// Logisim project Aria-1.circ as structural Verilog: 1 circuit, main circuit main
module main (
);

  wire adder_1_cout, and_3_out, clock_1_out, decoder_1_out1, decoder_1_out2, decoder_1_out6, decoder_1_out7,
       decoder_1_out8, decoder_1_out9, decoder_1_out10, decoder_1_out11, decoder_1_out12, decoder_1_out13,
       decoder_1_out14, decoder_1_out15, demultiplexer_1_out0, demultiplexer_1_out1, demultiplexer_1_out2,
       demultiplexer_1_out3, demultiplexer_1_out4, demultiplexer_1_out5, demultiplexer_1_out6,
       demultiplexer_1_out7, demultiplexer_1_out8, demultiplexer_1_out9, demultiplexer_1_out10,
       demultiplexer_1_out11, demultiplexer_1_out12, demultiplexer_1_out13, demultiplexer_1_out15, not_2_out,
       or_1_out, or_3_out, or_4_out, or_5_out, or_6_out, RESET_out, subtractor_1_bout, TICK_out, xor_2_out;
  wire [0:0] nor_1_out;
  wire [1:0] multiplexer_5_out;
  wire [2:2] multiplexer_4_out;
  wire [3:0] multiplexer_6_out, rom_1_data;
  wire [7:0] A_q, adder_1_out, adder_2_out, and_1_out, and_2_out, B_q, C_q, D_q, E_q, F_q, FL_q, G_q, H_q,
       I_q, IP_q, J_q, K_q, L_q, M_q, multiplexer_1_out, multiplexer_2_out, multiplexer_3_out,
       multiplexer_7_out, multiplexer_8_out, multiplexer_9_out, multiplexer_10_out, multiplexer_11_out,
       multiplexer_12_out, multiplexer_13_out, N_q, not_1_out, or_2_out, ram_1_data, rom_1_data_2,
       shifter_1_out, shifter_2_out, subtractor_1_out, xor_1_out;

  Multiplexer #(.width(8), .enable("false")) multiplexer_1 (
    .in0(multiplexer_13_out), .in1({{5{rom_1_data_2[3]}}, rom_1_data_2[2:0]}), .out(multiplexer_1_out),
    .sel(decoder_1_out6));
  // Probe on {{5{rom_1_data_2[3]}}, rom_1_data_2[2:0]}
  Adder adder_1 (.a(multiplexer_12_out), .b(multiplexer_1_out), .out(adder_1_out), .cout(adder_1_cout));  // open: cin
  or or_1 (or_1_out, adder_1_cout, subtractor_1_bout);
  ROM #(.dataWidth(12)) rom_1 (.addr(IP_q), .data({rom_1_data, rom_1_data_2}));  // open: sel
  ROM #(.dataWidth(12)) rom_2 ();  // open: addr, data, sel
  Subtractor subtractor_1 (
    .a(multiplexer_12_out), .b(multiplexer_13_out), .out(subtractor_1_out), .bout(subtractor_1_bout));  // open: bin
  assign not_1_out = ~multiplexer_12_out;  // NOT_Gate not_1, 8 bits wide
  // Probe on multiplexer_12_out
  // Probe on rom_1_data
  assign and_1_out = multiplexer_12_out & multiplexer_13_out;  // AND_Gate and_1, 8 bits wide
  Multiplexer #(.select(4), .width(8), .enable("false")) multiplexer_2 (
    .in0({8{1'b0}}), .in1({8{1'b0}}), .in2({8{1'b0}}), .in3({8{1'b0}}), .in4({8{1'b0}}), .in5({8{1'b0}}),
    .in6(adder_1_out), .in7(shifter_2_out), .in8(adder_1_out), .in9(subtractor_1_out), .in10(not_1_out),
    .in11(and_1_out), .in12(or_2_out), .in13(xor_1_out), .in14(shifter_1_out), .in15(shifter_2_out),
    .out(multiplexer_2_out), .sel(rom_1_data));
  Decoder #(.select(4), .disabled(0), .enable("false")) decoder_1 (
    .out1(decoder_1_out1), .out2(decoder_1_out2), .out6(decoder_1_out6), .out7(decoder_1_out7),
    .out8(decoder_1_out8), .out9(decoder_1_out9), .out10(decoder_1_out10), .out11(decoder_1_out11),
    .out12(decoder_1_out12), .out13(decoder_1_out13), .out14(decoder_1_out14), .out15(decoder_1_out15),
    .sel(rom_1_data));  // open: out0, out3, out4, out5
  // Probe on rom_1_data_2[3:0]
  // Probe on rom_1_data_2[7:4]
  assign xor_1_out = multiplexer_12_out ^ multiplexer_13_out;  // XOR_Gate xor_1, 8 bits wide
  assign or_2_out = multiplexer_12_out | multiplexer_13_out;  // OR_Gate or_2, 8 bits wide
  // Probe on ram_1_data
  RAM #(.bus("separate")) ram_1 (
    .addr(multiplexer_12_out), .din(multiplexer_13_out), .data(ram_1_data), .str(decoder_1_out2), .sel(1'b1),
    .clk(and_3_out), .ld(decoder_1_out1), .clr(RESET_out));
  or or_3 (or_3_out, or_5_out, decoder_1_out10, decoder_1_out11, decoder_1_out12, decoder_1_out13, decoder_1_out14, decoder_1_out15);
  // Probe on FL_q[0]
  // Probe on FL_q[1]
  // Probe on FL_q[2]
  Multiplexer #(.width(8), .enable("false")) multiplexer_3 (
    .in0(multiplexer_2_out), .in1(and_2_out), .out(multiplexer_3_out), .sel(decoder_1_out7));
  assign and_2_out = multiplexer_2_out & 8'h1;  // AND_Gate and_2, 8 bits wide
  or or_4 (or_4_out, decoder_1_out6, decoder_1_out7, or_3_out);
  or or_5 (or_5_out, decoder_1_out8, decoder_1_out9);
  Shifter shifter_1 (.in(multiplexer_12_out), .\dist (multiplexer_13_out[2:0]), .out(shifter_1_out));
  nor nor_1 (nor_1_out[0], multiplexer_2_out[0], multiplexer_2_out[1], multiplexer_2_out[2], multiplexer_2_out[3], multiplexer_2_out[4], multiplexer_2_out[5], multiplexer_2_out[6], multiplexer_2_out[7]);
  Shifter #(.shift("lr")) shifter_2 (.in(multiplexer_12_out), .\dist (multiplexer_13_out[2:0]), .out(shifter_2_out));
  Multiplexer #(.enable("false")) multiplexer_4 (
    .in0(FL_q[2]), .in1(or_1_out), .out(multiplexer_4_out[2]), .sel(or_5_out));
  Multiplexer #(.width(2), .enable("false")) multiplexer_5 (
    .in0(FL_q[1:0]), .in1({multiplexer_2_out[7], nor_1_out[0]}), .out(multiplexer_5_out), .sel(or_4_out));
  xor xor_2 (xor_2_out, FL_q[1], FL_q[2]);
  Multiplexer #(.select(4), .width(4), .enable("false")) multiplexer_6 (
    .in0(4'b0000), .in1(rom_1_data_2[7:4]), .in2(4'b0000), .in3(rom_1_data_2[7:4]), .in4(4'b1111),
    .in5(4'b1111), .in6(rom_1_data_2[7:4]), .in7(rom_1_data_2[7:4]), .in8(rom_1_data_2[7:4]),
    .in9(rom_1_data_2[7:4]), .in10(rom_1_data_2[7:4]), .in11(rom_1_data_2[7:4]), .in12(rom_1_data_2[7:4]),
    .in13(rom_1_data_2[7:4]), .in14(rom_1_data_2[7:4]), .in15(rom_1_data_2[7:4]), .out(multiplexer_6_out),
    .sel(rom_1_data));
  Multiplexer #(.width(8), .enable("false")) multiplexer_7 (
    .in0(rom_1_data_2), .in1(adder_2_out), .out(multiplexer_7_out), .sel(xor_2_out));
  // Probe on multiplexer_12_out
  // Probe on multiplexer_13_out
  // Probe on rom_1_data_2
  Multiplexer #(.width(8), .enable("false")) multiplexer_8 (
    .in0(adder_2_out), .in1(rom_1_data_2), .out(multiplexer_8_out), .sel(FL_q[0]));
  Clock clock_1 (.out(clock_1_out));
  or or_6 (or_6_out, clock_1_out, TICK_out);
  Button TICK (.out(TICK_out));
  Demultiplexer #(.select(4), .disabled(0), .enable("false")) demultiplexer_1 (
    .out0(demultiplexer_1_out0), .out1(demultiplexer_1_out1), .out2(demultiplexer_1_out2),
    .out3(demultiplexer_1_out3), .out4(demultiplexer_1_out4), .out5(demultiplexer_1_out5),
    .out6(demultiplexer_1_out6), .out7(demultiplexer_1_out7), .out8(demultiplexer_1_out8),
    .out9(demultiplexer_1_out9), .out10(demultiplexer_1_out10), .out11(demultiplexer_1_out11),
    .out12(demultiplexer_1_out12), .out13(demultiplexer_1_out13), .out15(demultiplexer_1_out15),
    .in(not_2_out), .sel(multiplexer_6_out));  // open: out14
  // Probe on multiplexer_6_out
  Multiplexer #(.select(4), .width(8), .enable("false")) multiplexer_9 (
    .in0(rom_1_data_2), .in1(ram_1_data), .in3(multiplexer_13_out), .in4(multiplexer_7_out),
    .in5(multiplexer_8_out), .in6(multiplexer_3_out), .in7(multiplexer_3_out), .in8(multiplexer_3_out),
    .in9(multiplexer_3_out), .in10(multiplexer_3_out), .in11(multiplexer_3_out), .in12(multiplexer_3_out),
    .in13(multiplexer_3_out), .in14(multiplexer_3_out), .in15(multiplexer_3_out), .out(multiplexer_9_out),
    .sel(rom_1_data));  // open: in2
  not not_2 (not_2_out, decoder_1_out2);
  and and_3 (and_3_out, or_6_out, ~RESET_out);  // AND_Gate
  Adder adder_2 (.a(IP_q), .b(8'h1), .out(adder_2_out));  // open: cin, cout
  Register A (.D(multiplexer_9_out), .en(demultiplexer_1_out0), .Q(A_q), .clk(and_3_out), .clr(RESET_out));
  Register B (.D(multiplexer_9_out), .en(demultiplexer_1_out1), .Q(B_q), .clk(and_3_out), .clr(RESET_out));
  Register C (.D(multiplexer_9_out), .en(demultiplexer_1_out2), .Q(C_q), .clk(and_3_out), .clr(RESET_out));
  Register D (.D(multiplexer_9_out), .en(demultiplexer_1_out3), .Q(D_q), .clk(and_3_out), .clr(RESET_out));
  Register E (.D(multiplexer_9_out), .en(demultiplexer_1_out4), .Q(E_q), .clk(and_3_out), .clr(RESET_out));
  Register F (.D(multiplexer_9_out), .en(demultiplexer_1_out5), .Q(F_q), .clk(and_3_out), .clr(RESET_out));
  Register G (.D(multiplexer_9_out), .en(demultiplexer_1_out6), .Q(G_q), .clk(and_3_out), .clr(RESET_out));
  Register H (.D(multiplexer_9_out), .en(demultiplexer_1_out7), .Q(H_q), .clk(and_3_out), .clr(RESET_out));
  Register I (.D(multiplexer_9_out), .en(demultiplexer_1_out8), .Q(I_q), .clk(and_3_out), .clr(RESET_out));
  Register J (.D(multiplexer_9_out), .en(demultiplexer_1_out9), .Q(J_q), .clk(and_3_out), .clr(RESET_out));
  Register K (.D(multiplexer_9_out), .en(demultiplexer_1_out10), .Q(K_q), .clk(and_3_out), .clr(RESET_out));
  Register L (.D(multiplexer_9_out), .en(demultiplexer_1_out11), .Q(L_q), .clk(and_3_out), .clr(RESET_out));
  Register M (.D(multiplexer_9_out), .en(demultiplexer_1_out12), .Q(M_q), .clk(and_3_out), .clr(RESET_out));
  Register N (.D(multiplexer_9_out), .en(demultiplexer_1_out13), .Q(N_q), .clk(and_3_out), .clr(RESET_out));
  Multiplexer #(.width(8), .enable("false")) multiplexer_10 (
    .in0(FL_q), .in1({{5{1'b0}}, multiplexer_4_out[2], multiplexer_5_out}), .out(multiplexer_10_out),
    .sel(or_4_out));
  Register FL (.D(multiplexer_10_out), .en(1'b1), .Q(FL_q), .clk(and_3_out), .clr(RESET_out));
  Register IP (.D(multiplexer_11_out), .en(1'b1), .Q(IP_q), .clk(and_3_out), .clr(RESET_out));
  Multiplexer #(.width(8), .enable("false")) multiplexer_11 (
    .in0(adder_2_out), .in1(multiplexer_9_out), .out(multiplexer_11_out), .sel(demultiplexer_1_out15));
  Button RESET (.out(RESET_out));
  Counter #(.width(12), .max('hfff)) Cycles (.clk(and_3_out), .clr(RESET_out));  // open: load, D, count, Q, carry
  Multiplexer #(.select(4), .width(8), .enable("false")) multiplexer_12 (
    .in0(A_q), .in1(B_q), .in2(C_q), .in3(D_q), .in4(E_q), .in5(F_q), .in6(G_q), .in7(H_q), .in8(I_q),
    .in9(J_q), .in10(K_q), .in11(L_q), .in12(M_q), .in13(N_q), .in14(FL_q), .in15(IP_q),
    .out(multiplexer_12_out), .sel(rom_1_data_2[7:4]));
  Multiplexer #(.select(4), .width(8), .enable("false")) multiplexer_13 (
    .in0(A_q), .in1(B_q), .in2(C_q), .in3(D_q), .in4(E_q), .in5(F_q), .in6(G_q), .in7(H_q), .in8(I_q),
    .in9(J_q), .in10(K_q), .in11(L_q), .in12(M_q), .in13(N_q), .in14(FL_q), .in15(IP_q),
    .out(multiplexer_13_out), .sel(rom_1_data_2[3:0]));

  // Notes on the sheet:
  //   Clock
  //   imm8
  //   contents of rom_1 (hex, n*v repeats v):
  //   d11 d44 1 320 242 641 e 904 50f 331 832 312 323 4 3f0 10 3f0 6 3f0 d00 204 16 3f0
  //   contents of rom_2 (hex, n*v repeats v):
  //   2b 310 5 320 d44 d55 332 735 a33 631 b31 e35 843 651 365 668 513 6 3f0 d00 204 16 3f0
  //   imm4
  //   Z
  //   S
  //   O
  //   ALU Output
  //   Reg write enable
  //   Reg write addr
  //   Reg write data
endmodule
